# Fritzing sketch scheme (saved by Fritzing 0.9.4)

parts:
  Part1 = Arduino Nano (Rev3.0)
  LCM1602_IIC1 = LCM1602 IIC [part_number="LCM1602 IIC" chip_label="LCM1602 IIC" package="DIP (Dual Inline) [THT]"]
  LCD1 = LCD screen
  BMP280_Breakout1 = BMP280 Breakout Board [part_number=BMP280]
  A1 = DHT22 module

nets:
  N1: Part1.D8, A1.DAT
  N2: Part1.D10, BMP280_Breakout1.CSB
  N3: Part1.D11/MOSI, BMP280_Breakout1.SDA
  N4: Part1.D12/MISO, BMP280_Breakout1.SDO
  GND: Part1.GND, LCM1602_IIC1.GND, BMP280_Breakout1.GND, A1.GND
  VCC: Part1.5V, LCM1602_IIC1.VCC, A1.VCC
  N5: Part1.A5, LCM1602_IIC1.SCL
  N6: Part1.A4, LCM1602_IIC1.SDA
  3V3: Part1.3V3, BMP280_Breakout1.VCC
  N7: Part1.D13/SCK, BMP280_Breakout1.SCL
  VSS: LCM1602_IIC1.VSS, LCD1.VSS
  VDD: LCM1602_IIC1.VDD, LCD1.VDD
  N8: LCM1602_IIC1.V0, LCD1.V0
  N9: LCM1602_IIC1.RS, LCD1.RS
  N10: LCM1602_IIC1.RW, LCD1.R/W
  N11: LCM1602_IIC1.E, LCD1.E
  N12: LCM1602_IIC1.D0, LCD1.DB0
  N13: LCM1602_IIC1.D1, LCD1.DB1
  N14: LCM1602_IIC1.D2, LCD1.DB2
  N15: LCM1602_IIC1.D3, LCD1.DB3
  N16: LCM1602_IIC1.D4, LCD1.DB4
  N17: LCM1602_IIC1.D5, LCD1.DB5
  N18: LCM1602_IIC1.D6, LCD1.DB6
  N19: LCM1602_IIC1.D7, LCD1.DB7
  N20: LCM1602_IIC1.A, LCD1.LED+
  N21: LCM1602_IIC1.K, LCD1.LED-

custom parts:
  LCM1602 IIC: I2C-Module to use a 1602 or 2004 LCD on with the wire.h libory Serial LCD Modul
  BMP280 Breakout Board: This is a breakout board for the Bosch Sensortec BMP280, "an absolute barometric pressure sensor especially designed for mobile applications." The operation range is 300 to 1100 hPa. Supply voltage is 1.2 to 3.6V. Operating temperature range is -40 to +85 °C.
  DHT22 module: DHT22 module. Pins GND VCC Data.
